// Logisim project MyProcessor2.circ as structural Verilog: 17 circuits, main circuit Processor
module Processor (
  input  Reset,
  input  [3:0] Display_Address
);

  wire alu_1_is, alu_1_is_2, bstall, bubble, Clock, control_unit_1_isbeq, control_unit_1_isbgt,
       control_unit_1_iscall, control_unit_1_isimmediate, control_unit_1_isld, control_unit_1_isret,
       control_unit_1_isst, control_unit_1_isubranch, control_unit_1_iswb, ex_malatch_1_iscall_2,
       ex_malatch_1_isld_2, ex_malatch_1_isst_2, ex_malatch_1_iswb_2, flags_1_flags_e, flags_1_flags_gt,
       isbranchTaken, isWb, MUX1, MUX2, MUX5, MUX6, not_1_out, of_exlatch_1_isbeq_2, of_exlatch_1_isbgt_2,
       of_exlatch_1_iscall_2, of_exlatch_1_isld_2, of_exlatch_1_isret_2, of_exlatch_1_isst_2,
       of_exlatch_1_isubranch_2, of_exlatch_1_iswb_2, stall;
  wire [1:0] ma_rwlatch_1_isld_2, MUX3, MUX4;
  wire [3:0] address, multiplexer_8_out, multiplexer_13_out;
  wire [12:0] control_unit_1_alusignals, of_exlatch_1_alusignals_2;
  wire [26:0] multiplexer_7_out;
  wire [31:0] adder_1_out, adder_2_out, adder_3_out, alu_1_aluresult, aluResult, bit_extender_1_out,
       branchTarget, calculate_immediate_1_immx, data, display, ex_malatch_1_op2_2, ex_malatch_1_pc_2,
       if_oflatch_1_pc_of, Instruction_EX_MA, Instruction_IF_OF, Instruction_MA_RW, Instruction_OF_EX,
       ma_rwlatch_1_aluresult_2, ma_rwlatch_1_ldresult_2, ma_rwlatch_1_pc_2, memory_unit_1_ldresult,
       multiplexer_1_out, multiplexer_2_out, multiplexer_3_out, multiplexer_4_out, multiplexer_6_out,
       multiplexer_9_out, multiplexer_10_out, multiplexer_11_out, multiplexer_12_out, multiplexer_14_out,
       of_exlatch_1_a_2, of_exlatch_1_b_2, of_exlatch_1_branchtarget_2, of_exlatch_1_op2_2,
       of_exlatch_1_pc_2, PC_q, register_file_1_readd1, register_file_1_readd2, rom_1_data, shifter_1_out;
  wire [31:27] multiplexer_7_out_2;

  not not_1 (not_1_out, stall);
  IF_OFLatch if_oflatch_1 (
    .Instruction_IF(multiplexer_12_out), .Instruction_OF(Instruction_IF_OF), .PC_IF(PC_q),
    .PC_OF(if_oflatch_1_pc_of), .clk(Clock), .reset(Reset), .Stall(stall));
  Register #(.width(32), .trigger("falling")) PC (
    .D(multiplexer_1_out), .en(not_1_out), .Q(PC_q), .clk(Clock), .clr(Reset));
  OF_EXLatch of_exlatch_1 (
    .isRet(control_unit_1_isret), .branchTarget(multiplexer_3_out), .aluSignals(control_unit_1_alusignals),
    .A(multiplexer_14_out), .isBeq(control_unit_1_isbeq), .op2(multiplexer_9_out),
    .isBgt(control_unit_1_isbgt), .B(multiplexer_6_out), .isUBranch(control_unit_1_isubranch),
    .Instruction_OF({multiplexer_7_out_2, multiplexer_7_out}), .isLd(control_unit_1_isld),
    .PC(if_oflatch_1_pc_of), .isSt(control_unit_1_isst), .isCall(control_unit_1_iscall),
    .isWb(control_unit_1_iswb), .in_16(Clock), .isRet_2(of_exlatch_1_isret_2),
    .branchTarget_2(of_exlatch_1_branchtarget_2), .aluSignals_2(of_exlatch_1_alusignals_2),
    .A_2(of_exlatch_1_a_2), .isBeq_2(of_exlatch_1_isbeq_2), .op2_2(of_exlatch_1_op2_2),
    .isBgt_2(of_exlatch_1_isbgt_2), .B_2(of_exlatch_1_b_2), .isUBranch_2(of_exlatch_1_isubranch_2),
    .Instruction_EX(Instruction_OF_EX), .isLd_2(of_exlatch_1_isld_2), .PC_2(of_exlatch_1_pc_2),
    .isSt_2(of_exlatch_1_isst_2), .isCall_2(of_exlatch_1_iscall_2), .isWb_2(of_exlatch_1_iswb_2),
    .in_17(Reset));
  MA_RWLatch ma_rwlatch_1 (
    .aluResult(aluResult), .ldResult(memory_unit_1_ldresult), .isLd(ex_malatch_1_isld_2),
    .InstructionMA(Instruction_EX_MA), .isCall(ex_malatch_1_iscall_2), .PC(ex_malatch_1_pc_2),
    .isWb(ex_malatch_1_iswb_2), .in_8(Clock), .reset(Reset), .aluResult_2(ma_rwlatch_1_aluresult_2),
    .ldResult_2(ma_rwlatch_1_ldresult_2), .isLd_2(ma_rwlatch_1_isld_2[0]), .InstructionRW(Instruction_MA_RW),
    .isCall_2(ma_rwlatch_1_isld_2[1]), .PC_2(ma_rwlatch_1_pc_2), .isWb_2(isWb));
  Multiplexer #(.width(32), .enable("false")) multiplexer_1 (
    .in0(adder_1_out), .in1(branchTarget), .out(multiplexer_1_out), .sel(isbranchTaken));
  assign bit_extender_1_out = {{5{multiplexer_7_out[26]}}, multiplexer_7_out};  // Bit_Extender bit_extender_1
  Adder #(.width(32)) adder_1 (.a(32'h4), .b(PC_q), .out(adder_1_out));  // open: cin, cout
  Shifter #(.width(32)) shifter_1 (.in(bit_extender_1_out), .\dist (5'b00010), .out(shifter_1_out));
  Multiplexer #(.select(2), .width(32), .enable("false")) multiplexer_2 (
    .in0(of_exlatch_1_b_2), .in1(data), .in2(aluResult), .in3(aluResult), .out(multiplexer_2_out), .sel(MUX4));
  ALU alu_1 (
    .A(multiplexer_10_out), .B(multiplexer_2_out), .ALUsignals(of_exlatch_1_alusignals_2),
    .aluResult(alu_1_aluresult), .is(alu_1_is), .is_2(alu_1_is_2));
  EX_MALatch ex_malatch_1 (
    .aluResult(alu_1_aluresult), .isLd(of_exlatch_1_isld_2), .op2(multiplexer_4_out),
    .isSt(of_exlatch_1_isst_2), .InstructionEX(Instruction_OF_EX), .isCall(of_exlatch_1_iscall_2),
    .PC(of_exlatch_1_pc_2), .isWb(of_exlatch_1_iswb_2), .in_9(Clock), .reset(Reset), .aluResult_2(aluResult),
    .isLd_2(ex_malatch_1_isld_2), .op2_2(ex_malatch_1_op2_2), .isSt_2(ex_malatch_1_isst_2),
    .InstructionMA(Instruction_EX_MA), .isCall_2(ex_malatch_1_iscall_2), .PC_2(ex_malatch_1_pc_2),
    .isWb_2(ex_malatch_1_iswb_2));
  Adder #(.width(32)) adder_2 (.a(ma_rwlatch_1_pc_2), .b(32'h4), .out(adder_2_out));  // open: cin, cout
  Calculate_Immediate calculate_immediate_1 (.imm(multiplexer_7_out[17:0]), .immx(calculate_immediate_1_immx));
  Adder #(.width(32)) adder_3 (.a(shifter_1_out), .b(if_oflatch_1_pc_of), .out(adder_3_out));  // open: cin, cout
  Multiplexer #(.width(32), .enable("false")) multiplexer_3 (
    .in0(adder_3_out), .in1(register_file_1_readd1), .out(multiplexer_3_out), .sel(control_unit_1_isret));
  Multiplexer #(.width(32), .enable("false")) multiplexer_4 (
    .in0(of_exlatch_1_op2_2), .in1(data), .out(multiplexer_4_out), .sel(MUX5));
  Multiplexer #(.select(2), .width(32), .enable("false")) multiplexer_5 (
    .in0(ma_rwlatch_1_aluresult_2), .in1(ma_rwlatch_1_ldresult_2), .in2(adder_2_out), .out(data),
    .sel(ma_rwlatch_1_isld_2));  // open: in3
  Multiplexer #(.width(32), .enable("false")) multiplexer_6 (
    .in0(multiplexer_9_out), .in1(calculate_immediate_1_immx), .out(multiplexer_6_out),
    .sel(control_unit_1_isimmediate));
  Flags flags_1 (
    .isCmp(of_exlatch_1_alusignals_2[0]), .is(alu_1_is), .is_2(alu_1_is_2), .flags_GT(flags_1_flags_gt),
    .flags_E(flags_1_flags_e));
  Memory_Unit memory_unit_1 (
    .MAR(aluResult), .ldResult(memory_unit_1_ldresult), .MDR(multiplexer_11_out), .isSt(ex_malatch_1_isst_2),
    .isLd(ex_malatch_1_isld_2), .Clock(Clock), .Reset(Reset));
  ROM #(.addrWidth(24), .dataWidth(32)) rom_1 (.addr(PC_q[25:2]), .data(rom_1_data));  // open: sel
  Multiplexer #(.width(32), .enable("false")) multiplexer_7 (
    .in0(Instruction_IF_OF), .in1(32'h68000000), .out({multiplexer_7_out_2, multiplexer_7_out}), .sel(bstall));
  Multiplexer #(.width(4), .enable("false")) multiplexer_8 (
    .in0(multiplexer_7_out[17:14]), .in1(multiplexer_7_out[25:22]), .out(multiplexer_8_out),
    .sel(control_unit_1_isst));
  Multiplexer #(.width(32), .enable("false")) multiplexer_9 (
    .in0(register_file_1_readd2), .in1(data), .out(multiplexer_9_out), .sel(MUX2));
  Multiplexer #(.select(2), .width(32), .enable("false")) multiplexer_10 (
    .in0(of_exlatch_1_a_2), .in1(data), .in2(aluResult), .in3(aluResult), .out(multiplexer_10_out), .sel(MUX3));
  Multiplexer #(.width(32), .enable("false")) multiplexer_11 (
    .in0(ex_malatch_1_op2_2), .in1(data), .out(multiplexer_11_out), .sel(MUX6));
  Multiplexer #(.width(32), .enable("false")) multiplexer_12 (
    .in0(rom_1_data), .in1(32'h68000000), .out(multiplexer_12_out), .sel(bubble));
  Multiplexer #(.width(4), .enable("false")) multiplexer_13 (
    .in0(multiplexer_7_out[21:18]), .in1(4'b1111), .out(multiplexer_13_out), .sel(control_unit_1_isret));
  Multiplexer #(.width(32), .enable("false")) multiplexer_14 (
    .in0(register_file_1_readd1), .in1(data), .out(multiplexer_14_out), .sel(MUX1));
  Multiplexer #(.width(32), .enable("false")) multiplexer_15 (
    .in0(of_exlatch_1_branchtarget_2), .in1(multiplexer_10_out), .out(branchTarget),
    .sel(of_exlatch_1_isret_2));
  Clock u_Clock (.out(Clock));
  Register_File register_file_1 (
    .ReadA1(multiplexer_13_out), .ReadA2(multiplexer_8_out), .WriteE(isWb), .WriteD(data),
    .ReadD1(register_file_1_readd1), .ReadD2(register_file_1_readd2), .Clock(Clock), .Reset(Reset),
    .DisplayD(display), .DisplayA(Display_Address), .WriteA(address));
  Branch_Unit branch_unit_1 (
    .isBeq(of_exlatch_1_isbeq_2), .isUBranch(of_exlatch_1_isubranch_2), .flags_E(flags_1_flags_e),
    .isBgt(of_exlatch_1_isbgt_2), .flags_GT(flags_1_flags_gt), .isBranchTaken(isbranchTaken));
  Multiplexer #(.width(4), .enable("false")) multiplexer_16 (
    .in0(Instruction_MA_RW[25:22]), .in1(4'b1111), .out(address), .sel(ma_rwlatch_1_isld_2[1]));
  Control_Unit control_unit_1 (
    .isSt(control_unit_1_isst), .isLd(control_unit_1_isld), .isBeq(control_unit_1_isbeq),
    .isBgt(control_unit_1_isbgt), .isRet(control_unit_1_isret), .I_bit(multiplexer_7_out[26]),
    .isImmediate(control_unit_1_isimmediate), .opcode(multiplexer_7_out_2), .isWb(control_unit_1_iswb),
    .isUbranch(control_unit_1_isubranch), .isCall(control_unit_1_iscall),
    .ALUsignals(control_unit_1_alusignals));
  Hex_Digit_Display hex_digit_display_1 (.value(display[31:28]));  // open: dp
  Hex_Digit_Display hex_digit_display_2 (.value(display[27:24]));  // open: dp
  Hex_Digit_Display hex_digit_display_3 (.value(display[19:16]));  // open: dp
  Hex_Digit_Display hex_digit_display_4 (.value(display[23:20]));  // open: dp
  Hex_Digit_Display hex_digit_display_5 (.value(display[15:12]));  // open: dp
  Hex_Digit_Display hex_digit_display_6 (.value(display[11:8]));  // open: dp
  or or_1 (bstall, stall, bubble);
  Hex_Digit_Display hex_digit_display_7 (.value(display[3:0]));  // open: dp
  Hex_Digit_Display hex_digit_display_8 (.value(display[7:4]));  // open: dp
  Hex_Digit_Display hex_digit_display_9 (.value(Instruction_IF_OF[31:28]));  // open: dp
  Hex_Digit_Display hex_digit_display_10 (.value(Instruction_OF_EX[31:28]));  // open: dp
  Hex_Digit_Display hex_digit_display_11 (.value(Instruction_EX_MA[31:28]));  // open: dp
  Hex_Digit_Display hex_digit_display_12 (.value(Instruction_MA_RW[31:28]));  // open: dp
  Hex_Digit_Display hex_digit_display_13 (.value(Instruction_IF_OF[27:24]));  // open: dp
  Hex_Digit_Display hex_digit_display_14 (.value(Instruction_IF_OF[23:20]));  // open: dp
  Hex_Digit_Display hex_digit_display_15 (.value(Instruction_OF_EX[27:24]));  // open: dp
  Hex_Digit_Display hex_digit_display_16 (.value(Instruction_OF_EX[23:20]));  // open: dp
  Hex_Digit_Display hex_digit_display_17 (.value(Instruction_EX_MA[23:20]));  // open: dp
  Hex_Digit_Display hex_digit_display_18 (.value(Instruction_EX_MA[27:24]));  // open: dp
  Hex_Digit_Display hex_digit_display_19 (.value(Instruction_MA_RW[23:20]));  // open: dp
  Hex_Digit_Display hex_digit_display_20 (.value(Instruction_MA_RW[27:24]));  // open: dp
  Forwarding_Unit forwarding_unit_1 (
    .InstrIF_OF(Instruction_IF_OF), .InstrOF_EX(Instruction_OF_EX), .InstrEX_MA(Instruction_EX_MA),
    .InstrMA_RW(Instruction_MA_RW), .Mux1(MUX1), .Mux2(MUX2), .Mux3(MUX3), .Mux4(MUX4), .Mux5(MUX5),
    .Mux6(MUX6));
  Hex_Digit_Display hex_digit_display_21 (.value(Instruction_IF_OF[15:12]));  // open: dp
  Hex_Digit_Display hex_digit_display_22 (.value(Instruction_IF_OF[19:16]));  // open: dp
  Hex_Digit_Display hex_digit_display_23 (.value(Instruction_OF_EX[19:16]));  // open: dp
  Hex_Digit_Display hex_digit_display_24 (.value(Instruction_OF_EX[15:12]));  // open: dp
  Hex_Digit_Display hex_digit_display_25 (.value(Instruction_EX_MA[15:12]));  // open: dp
  Hex_Digit_Display hex_digit_display_26 (.value(Instruction_EX_MA[19:16]));  // open: dp
  Hex_Digit_Display hex_digit_display_27 (.value(Instruction_MA_RW[15:12]));  // open: dp
  Hex_Digit_Display hex_digit_display_28 (.value(Instruction_MA_RW[19:16]));  // open: dp
  Branch_Lock_Unit branch_lock_unit_1 (.isBranchTaken(isbranchTaken), .bubble(bubble));
  Data_Lock_Unit data_lock_unit_1 (.InstrIF_OF(Instruction_IF_OF), .InstrOF_EX(Instruction_OF_EX), .Stall(stall));
  Hex_Digit_Display hex_digit_display_29 (.value(Instruction_IF_OF[11:8]));  // open: dp
  Hex_Digit_Display hex_digit_display_30 (.value(Instruction_IF_OF[7:4]));  // open: dp
  Hex_Digit_Display hex_digit_display_31 (.value(Instruction_OF_EX[7:4]));  // open: dp
  Hex_Digit_Display hex_digit_display_32 (.value(Instruction_OF_EX[11:8]));  // open: dp
  Hex_Digit_Display hex_digit_display_33 (.value(Instruction_EX_MA[11:8]));  // open: dp
  Hex_Digit_Display hex_digit_display_34 (.value(Instruction_EX_MA[7:4]));  // open: dp
  Hex_Digit_Display hex_digit_display_35 (.value(Instruction_MA_RW[7:4]));  // open: dp
  Hex_Digit_Display hex_digit_display_36 (.value(Instruction_MA_RW[11:8]));  // open: dp
  Hex_Digit_Display hex_digit_display_37 (.value(Instruction_IF_OF[3:0]));  // open: dp
  Hex_Digit_Display hex_digit_display_38 (.value(Instruction_OF_EX[3:0]));  // open: dp
  Hex_Digit_Display hex_digit_display_39 (.value(Instruction_EX_MA[3:0]));  // open: dp
  Hex_Digit_Display hex_digit_display_40 (.value(Instruction_MA_RW[3:0]));  // open: dp

  // Notes on the sheet:
  //   PC
  //   PC
  //   PC
  //   PC
  //   ALUsignals
  //   aluResult
  //   aluResult
  //   pc
  //   pc+4
  //   isBranchTaken
  //   branchTarget
  //   pc
  //   branchTarget
  //   B
  //   B
  //   B
  //   ALU
  //   aluResult
  //   MAR
  //   imm
  //   offset
  //   instruction
  //   op2
  //   op2
  //   A
  //   is>
  //   is=
  //   MDR
  //   Memory
  //   Unit
  //   ldResult
  //   ldResult
  //   data
  //   Instruction Memory
  //   calc immx
  //   immx
  //   isRet
  //   Flags
  //   isCmp
  //   op2
  //   isLd
  //   isSt
  //   isLd
  //   isCall
  //   5 STAGE PIPELINED PROCESSOR
  //   Mohammad Yusuf 2023EET2757
  //   contents of rom_1 (hex, n*v repeats v):
  //   4c00000a 98000002 90000000 2c000001 88000003 4c400001 a0000000 fb80008 7c380000 7ff80004 c000001
  //   9ffffff8 77f80004 74380000 7b80008 10404000 a0000000
  //   instruction
  //   rs2
  //   rd
  //   op2
  //   A
  //   A
  //   branchTarget
  //   flags(GT)
  //   flags(E)
  //   op2
  //   Instruction
  //   rs1
  //   isSt
  //   E
  //   Register
  //   A
  //   File
  //   D
  //   op1
  //   Branch
  //   Unit
  //   isRet
  //   isWb
  //   address
  //   data
  //   isRet
  //   isBeq
  //   isBgt
  //   isUBranch
  //   rd
  //   opcode
  //   CONTROL
  //   I bit
  //   UNIT
  //   isImmediate
  //   instruction
  //   instruction
  //   Instruction IF-OF Latch
  //   Instruction OF-EX Latch
  //   Instruction EX-MA Latch
  //   Instruction MA-RW Latch
  //   Display Register
  //   Display Register
  //   Display Register
  //   Display Register
  //   Display Register
endmodule

module Control_Unit (
  input  I_bit,
  input  [4:0] opcode,
  output isSt,
  output isLd,
  output isBeq,
  output isBgt,
  output isRet,
  output isImmediate,
  output isWb,
  output isUbranch,
  output isCall,
  output [12:0] ALUsignals
);

  wire and_6_out, and_7_out, and_8_out, and_9_out, and_10_out, and_12_out, and_13_out, nand_1_out;

  nand nand_1 (nand_1_out, opcode[0], opcode[1]);
  and and_1 (isSt, opcode[0], opcode[1], opcode[2], opcode[3], ~opcode[4]);  // AND_Gate
  and and_2 (isLd, ~opcode[0], opcode[1], opcode[2], opcode[3], ~opcode[4]);  // AND_Gate
  and and_3 (isBeq, ~opcode[0], ~opcode[1], ~opcode[2], ~opcode[3], opcode[4]);  // AND_Gate
  and and_4 (isBgt, opcode[0], ~opcode[1], ~opcode[2], ~opcode[3], opcode[4]);  // AND_Gate
  and and_5 (isRet, ~opcode[0], ~opcode[1], opcode[2], ~opcode[3], opcode[4]);  // AND_Gate
  and and_6 (and_6_out, opcode[0], ~opcode[1], opcode[2], ~opcode[4]);  // AND_Gate
  and and_7 (and_7_out, opcode[0], opcode[2], opcode[3], ~opcode[4]);  // AND_Gate
  and and_8 (and_8_out, opcode[4], nand_1_out);
  and and_9 (and_9_out, opcode[1], ~opcode[2], ~opcode[3], opcode[4]);  // AND_Gate
  and and_10 (and_10_out, ~opcode[0], ~opcode[1], opcode[2], ~opcode[3], opcode[4]);  // AND_Gate
  and and_11 (isCall, opcode[0], opcode[1], ~opcode[2], ~opcode[3], opcode[4]);  // AND_Gate
  and and_12 (and_12_out, ~opcode[0], ~opcode[1], ~opcode[2], ~opcode[3], ~opcode[4]);  // AND_Gate
  and and_13 (and_13_out, opcode[1], opcode[2], opcode[3], ~opcode[4]);  // AND_Gate
  and isSub (ALUsignals[2], opcode[0], ~opcode[1], ~opcode[2], ~opcode[3], ~opcode[4]);  // AND_Gate
  and isCmp (ALUsignals[0], opcode[0], ~opcode[1], opcode[2], ~opcode[3], ~opcode[4]);  // AND_Gate
  and isMul (ALUsignals[3], ~opcode[0], opcode[1], ~opcode[2], ~opcode[3], ~opcode[4]);  // AND_Gate
  and isDiv (ALUsignals[4], opcode[0], opcode[1], ~opcode[2], ~opcode[3], ~opcode[4]);  // AND_Gate
  and isMod (ALUsignals[5], ~opcode[0], ~opcode[1], opcode[2], ~opcode[3], ~opcode[4]);  // AND_Gate
  and isLsl (ALUsignals[7], ~opcode[0], opcode[1], ~opcode[2], opcode[3], ~opcode[4]);  // AND_Gate
  and isLsr (ALUsignals[8], opcode[0], opcode[1], ~opcode[2], opcode[3], ~opcode[4]);  // AND_Gate
  and isAsr (ALUsignals[9], ~opcode[0], ~opcode[1], opcode[2], opcode[3], ~opcode[4]);  // AND_Gate
  and isOr (ALUsignals[12], opcode[0], opcode[1], opcode[2], ~opcode[3], ~opcode[4]);  // AND_Gate
  and isAnd (ALUsignals[11], ~opcode[0], opcode[1], opcode[2], ~opcode[3], ~opcode[4]);  // AND_Gate
  and isNot (ALUsignals[10], ~opcode[0], ~opcode[1], ~opcode[2], opcode[3], ~opcode[4]);  // AND_Gate
  and isMov (ALUsignals[6], opcode[0], ~opcode[1], ~opcode[2], opcode[3], ~opcode[4]);  // AND_Gate
  or or_1 (isUbranch, and_9_out, and_10_out);
  or isAdd (ALUsignals[1], and_12_out, and_13_out);
  nor nor_1 (isWb, and_6_out, and_7_out, and_8_out);

  assign isImmediate = I_bit;

  // Notes on the sheet:
  //   op1
  //   op2
  //   op3
  //   op4
  //   op5
endmodule

module Register_File (
  input  Clock,
  input  Reset,
  input  [31:0] WriteD,
  input  [3:0] ReadA1,
  input  WriteE,
  input  [3:0] WriteA,
  input  [3:0] ReadA2,
  input  [3:0] DisplayA,
  output [31:0] ReadD1,
  output [31:0] ReadD2,
  output [31:0] DisplayD
);

  wire demultiplexer_1_out0, demultiplexer_1_out1, demultiplexer_1_out2, demultiplexer_1_out3,
       demultiplexer_1_out4, demultiplexer_1_out5, demultiplexer_1_out6, demultiplexer_1_out7,
       demultiplexer_1_out8, demultiplexer_1_out9, demultiplexer_1_out10, demultiplexer_1_out11,
       demultiplexer_1_out12, demultiplexer_1_out13, demultiplexer_1_out14, demultiplexer_1_out15,
       multiplexer_2_out, or_1_out, or_2_out;
  wire [31:0] multiplexer_1_out, r0_q, r1_q, r2_q, r3_q, r4_q, r5_q, r6_q, r7_q, r8_q, r9_q, r10_q, r11_q,
       r12_q, r13_q, r14_q, r15_q;

  Demultiplexer #(.select(4), .disabled(0), .enable("false")) demultiplexer_1 (
    .out0(demultiplexer_1_out0), .out1(demultiplexer_1_out1), .out2(demultiplexer_1_out2),
    .out3(demultiplexer_1_out3), .out4(demultiplexer_1_out4), .out5(demultiplexer_1_out5),
    .out6(demultiplexer_1_out6), .out7(demultiplexer_1_out7), .out8(demultiplexer_1_out8),
    .out9(demultiplexer_1_out9), .out10(demultiplexer_1_out10), .out11(demultiplexer_1_out11),
    .out12(demultiplexer_1_out12), .out13(demultiplexer_1_out13), .out14(demultiplexer_1_out14),
    .out15(demultiplexer_1_out15), .in(WriteE), .sel(WriteA));
  Multiplexer #(.width(32), .enable("false")) multiplexer_1 (
    .in0(WriteD), .in1(32'h3fffffc), .out(multiplexer_1_out), .sel(Reset));
  or or_1 (or_1_out, demultiplexer_1_out14, Reset);
  Multiplexer #(.enable("false")) multiplexer_2 (.in0(or_2_out), .out(multiplexer_2_out), .sel(1'b0));  // open: in1
  or or_2 (or_2_out, Clock, Reset);
  Register #(.width(32)) r0 (.D(WriteD), .en(demultiplexer_1_out0), .Q(r0_q), .clk(Clock), .clr(Reset));
  Register #(.width(32)) r1 (.D(WriteD), .en(demultiplexer_1_out1), .Q(r1_q), .clk(Clock), .clr(Reset));
  Register #(.width(32)) r2 (.D(WriteD), .en(demultiplexer_1_out2), .Q(r2_q), .clk(Clock), .clr(Reset));
  Register #(.width(32)) r3 (.D(WriteD), .en(demultiplexer_1_out3), .Q(r3_q), .clk(Clock), .clr(Reset));
  Register #(.width(32)) r4 (.D(WriteD), .en(demultiplexer_1_out4), .Q(r4_q), .clk(Clock), .clr(Reset));
  Register #(.width(32)) r5 (.D(WriteD), .en(demultiplexer_1_out5), .Q(r5_q), .clk(Clock), .clr(Reset));
  Register #(.width(32)) r6 (.D(WriteD), .en(demultiplexer_1_out6), .Q(r6_q), .clk(Clock), .clr(Reset));
  Register #(.width(32)) r7 (.D(WriteD), .en(demultiplexer_1_out7), .Q(r7_q), .clk(Clock), .clr(Reset));
  Register #(.width(32)) r8 (.D(WriteD), .en(demultiplexer_1_out8), .Q(r8_q), .clk(Clock), .clr(Reset));
  Register #(.width(32)) r9 (.D(WriteD), .en(demultiplexer_1_out9), .Q(r9_q), .clk(Clock), .clr(Reset));
  Register #(.width(32)) r10 (.D(WriteD), .en(demultiplexer_1_out10), .Q(r10_q), .clk(Clock), .clr(Reset));
  Register #(.width(32)) r11 (.D(WriteD), .en(demultiplexer_1_out11), .Q(r11_q), .clk(Clock), .clr(Reset));
  Register #(.width(32)) r12 (.D(WriteD), .en(demultiplexer_1_out12), .Q(r12_q), .clk(Clock), .clr(Reset));
  Register #(.width(32)) r13 (.D(WriteD), .en(demultiplexer_1_out13), .Q(r13_q), .clk(Clock), .clr(Reset));
  Register #(.width(32)) r14 (.D(multiplexer_1_out), .en(or_1_out), .Q(r14_q), .clk(multiplexer_2_out));  // open: clr
  Register #(.width(32)) r15 (.D(WriteD), .en(demultiplexer_1_out15), .Q(r15_q), .clk(Clock), .clr(Reset));
  Multiplexer #(.select(4), .width(32), .disabled(0), .enable("false")) multiplexer_3 (
    .in0(r0_q), .in1(r1_q), .in2(r2_q), .in3(r3_q), .in4(r4_q), .in5(r5_q), .in6(r6_q), .in7(r7_q),
    .in8(r8_q), .in9(r9_q), .in10(r10_q), .in11(r11_q), .in12(r12_q), .in13(r13_q), .in14(r14_q),
    .in15(r15_q), .out(ReadD1), .sel(ReadA1));
  Multiplexer #(.select(4), .width(32), .disabled(0), .enable("false")) multiplexer_4 (
    .in0(r0_q), .in1(r1_q), .in2(r2_q), .in3(r3_q), .in4(r4_q), .in5(r5_q), .in6(r6_q), .in7(r7_q),
    .in8(r8_q), .in9(r9_q), .in10(r10_q), .in11(r11_q), .in12(r12_q), .in13(r13_q), .in14(r14_q),
    .in15(r15_q), .out(ReadD2), .sel(ReadA2));
  Multiplexer #(.select(4), .width(32), .disabled(0), .enable("false")) multiplexer_5 (
    .in0(r0_q), .in1(r1_q), .in2(r2_q), .in3(r3_q), .in4(r4_q), .in5(r5_q), .in6(r6_q), .in7(r7_q),
    .in8(r8_q), .in9(r9_q), .in10(r10_q), .in11(r11_q), .in12(r12_q), .in13(r13_q), .in14(r14_q),
    .in15(r15_q), .out(DisplayD), .sel(DisplayA));
endmodule

module ALU (
  input  [31:0] A,
  input  [31:0] B,
  input  [12:0] ALUsignals,
  output [31:0] aluResult,
  output is,
  output is_2
);

  wire [31:0] adder_1_out, and_1_out, divider_1_out, divider_1_rem, multiplier_1_out, not_1_out, or_1_out,
       shifter_1_out, shifter_2_out, shifter_3_out, subtractor_1_out;

  Adder #(.width(32)) adder_1 (.a(A), .b(B), .out(adder_1_out));  // open: cin, cout
  Subtractor #(.width(32)) subtractor_1 (.a(A), .b(B), .out(subtractor_1_out));  // open: bin, bout
  Multiplier #(.width(32)) multiplier_1 (.a(A), .b(B), .out(multiplier_1_out));  // open: cin, cout
  Divider #(.width(32)) divider_1 (.a(A), .b(B), .out(divider_1_out), .rem(divider_1_rem));  // open: upper
  Comparator #(.width(32)) comparator_1 (.a(A), .b(B), .gt(is), .eq(is_2));  // open: lt
  Shifter #(.width(32)) shifter_1 (.in(A), .\dist (B[4:0]), .out(shifter_1_out));
  Shifter #(.width(32), .shift("lr")) shifter_2 (.in(A), .\dist (B[4:0]), .out(shifter_2_out));
  Shifter #(.width(32), .shift("ar")) shifter_3 (.in(A), .\dist (B[4:0]), .out(shifter_3_out));
  assign not_1_out = ~B;  // NOT_Gate not_1, 32 bits wide
  assign and_1_out = A & B;  // AND_Gate and_1, 32 bits wide
  assign or_1_out = A | B;  // OR_Gate or_1, 32 bits wide
  assign aluResult = ALUsignals[1] ? adder_1_out : 32'bz;  // Controlled_Buffer controlled_buffer_1
  assign aluResult = ALUsignals[2] ? subtractor_1_out : 32'bz;  // Controlled_Buffer controlled_buffer_2
  assign aluResult = ALUsignals[3] ? multiplier_1_out : 32'bz;  // Controlled_Buffer controlled_buffer_3
  assign aluResult = ALUsignals[4] ? divider_1_out : 32'bz;  // Controlled_Buffer controlled_buffer_4
  assign aluResult = ALUsignals[5] ? divider_1_rem : 32'bz;  // Controlled_Buffer controlled_buffer_5
  assign aluResult = ALUsignals[6] ? B : 32'bz;  // Controlled_Buffer controlled_buffer_6
  assign aluResult = ALUsignals[7] ? shifter_1_out : 32'bz;  // Controlled_Buffer controlled_buffer_7
  assign aluResult = ALUsignals[8] ? shifter_2_out : 32'bz;  // Controlled_Buffer controlled_buffer_8
  assign aluResult = ALUsignals[9] ? shifter_3_out : 32'bz;  // Controlled_Buffer controlled_buffer_9
  assign aluResult = ALUsignals[10] ? not_1_out : 32'bz;  // Controlled_Buffer controlled_buffer_10
  assign aluResult = ALUsignals[11] ? and_1_out : 32'bz;  // Controlled_Buffer controlled_buffer_11
  assign aluResult = ALUsignals[12] ? or_1_out : 32'bz;  // Controlled_Buffer controlled_buffer_12

  // Notes on the sheet:
  //   add
  //   sub
  //   mul
  //   div
  //   cmp
  //   lsr
  //   mod
  //   lsl
  //   asr
endmodule

module Flags (
  input  isCmp,
  input  is,
  input  is_2,
  output flags_GT,
  output flags_E
);

  D_Flip_Flop #(.trigger("high")) d_ff_1 (.clk(isCmp), .D(is), .Q(flags_GT));  // open: Qn, preset, en, reset
  D_Flip_Flop #(.trigger("high")) d_ff_2 (.clk(isCmp), .D(is_2), .Q(flags_E));  // open: Qn, preset, en, reset
endmodule

module Branch_Unit (
  input  isUBranch,
  input  isBeq,
  input  flags_E,
  input  isBgt,
  input  flags_GT,
  output isBranchTaken
);

  wire and_1_out, and_2_out;

  and and_1 (and_1_out, isBeq, flags_E);
  and and_2 (and_2_out, isBgt, flags_GT);
  or or_1 (isBranchTaken, isUBranch, and_1_out, and_2_out);
endmodule

module Memory_Unit (
  input  [31:0] MAR,
  input  isLd,
  input  [31:0] MDR,
  input  isSt,
  input  Clock,
  input  Reset,
  output [31:0] ldResult
);

  RAM #(.addrWidth(24), .dataWidth(32), .bus("separate")) ram_1 (
    .addr(MAR[25:2]), .din(MDR), .data(ldResult), .str(isSt), .clk(Clock), .ld(isLd), .clr(Reset));  // open: sel
endmodule

module Calculate_Immediate (
  input  [17:0] imm,
  output [31:0] immx
);

  wire [31:0] bit_extender_1_out, bit_extender_2_out, shifter_1_out;

  assign bit_extender_1_out = {{16{1'b0}}, imm[15:0]};  // Bit_Extender bit_extender_1
  assign bit_extender_2_out = {{16{imm[15]}}, imm[15:0]};  // Bit_Extender bit_extender_2
  Shifter #(.width(32)) shifter_1 (.in(bit_extender_1_out), .\dist (5'b10000), .out(shifter_1_out));
  Multiplexer #(.select(2), .width(32), .enable("false")) multiplexer_1 (
    .in0(bit_extender_2_out), .in1(bit_extender_1_out), .in2(shifter_1_out), .out(immx), .sel(imm[17:16]));  // open: in3

  // Notes on the sheet:
  //   modifier bits
  //   high
  //   default
  //   unsigned
endmodule

// IF-OF LATCH
module IF_OFLatch (
  input  [31:0] Instruction_IF,
  input  [31:0] PC_IF,
  input  clk,
  input  reset,
  input  Stall,
  output [31:0] Instruction_OF,
  output [31:0] PC_OF
);

  wire not_1_out;

  not not_1 (not_1_out, Stall);
  Register #(.width(32), .trigger("falling")) register_1 (
    .D(Instruction_IF), .en(not_1_out), .Q(Instruction_OF), .clk(clk), .clr(reset));
  Register #(.width(32), .trigger("falling")) register_2 (.D(PC_IF), .en(not_1_out), .Q(PC_OF), .clk(clk), .clr(reset));
endmodule

module Branch_Lock_Unit (
  input  isBranchTaken,
  output bubble
);


  assign bubble = isBranchTaken;
endmodule

// OF-EX Latch
module OF_EXLatch (
  input  isRet,
  input  [31:0] branchTarget,
  input  [12:0] aluSignals,
  input  [31:0] A,
  input  isBeq,
  input  [31:0] op2,
  input  isBgt,
  input  [31:0] B,
  input  isUBranch,
  input  [31:0] Instruction_OF,
  input  isLd,
  input  [31:0] PC,
  input  isSt,
  input  isCall,
  input  isWb,
  input  in_16,
  input  in_17,
  output isRet_2,
  output [31:0] branchTarget_2,
  output [12:0] aluSignals_2,
  output [31:0] A_2,
  output isBeq_2,
  output [31:0] op2_2,
  output isBgt_2,
  output [31:0] B_2,
  output isUBranch_2,
  output [31:0] Instruction_EX,
  output isLd_2,
  output [31:0] PC_2,
  output isSt_2,
  output isCall_2,
  output isWb_2
);

  Register #(.width(32), .trigger("falling")) register_1 (
    .D(branchTarget), .Q(branchTarget_2), .clk(in_16), .clr(in_17));  // open: en
  Register #(.width(32), .trigger("falling")) register_2 (.D(A), .Q(A_2), .clk(in_16), .clr(in_17));  // open: en
  Register #(.width(32), .trigger("falling")) register_3 (.D(op2), .Q(op2_2), .clk(in_16), .clr(in_17));  // open: en
  Register #(.width(32), .trigger("falling")) register_4 (.D(B), .Q(B_2), .clk(in_16), .clr(in_17));  // open: en
  Register #(.width(32), .trigger("falling")) register_5 (
    .D(Instruction_OF), .Q(Instruction_EX), .clk(in_16), .clr(in_17));  // open: en
  Register #(.width(32), .trigger("falling")) register_6 (.D(PC), .Q(PC_2), .clk(in_16), .clr(in_17));  // open: en
  Register #(.width(1), .trigger("falling")) register_7 (.D(isRet), .Q(isRet_2), .clk(in_16), .clr(in_17));  // open: en
  Register #(.width(13), .trigger("falling")) register_8 (
    .D(aluSignals), .Q(aluSignals_2), .clk(in_16), .clr(in_17));  // open: en
  Register #(.width(1), .trigger("falling")) register_9 (.D(isBeq), .Q(isBeq_2), .clk(in_16), .clr(in_17));  // open: en
  Register #(.width(1), .trigger("falling")) register_10 (
    .D(isBgt), .Q(isBgt_2), .clk(in_16), .clr(in_17));  // open: en
  Register #(.width(1), .trigger("falling")) register_11 (
    .D(isUBranch), .Q(isUBranch_2), .clk(in_16), .clr(in_17));  // open: en
  Register #(.width(1), .trigger("falling")) register_12 (.D(isLd), .Q(isLd_2), .clk(in_16), .clr(in_17));  // open: en
  Register #(.width(1), .trigger("falling")) register_13 (.D(isSt), .Q(isSt_2), .clk(in_16), .clr(in_17));  // open: en
  Register #(.width(1), .trigger("falling")) register_14 (
    .D(isCall), .Q(isCall_2), .clk(in_16), .clr(in_17));  // open: en
  Register #(.width(1), .trigger("falling")) register_15 (.D(isWb), .Q(isWb_2), .clk(in_16), .clr(in_17));  // open: en
endmodule

// EX-MA Latch
module EX_MALatch (
  input  [31:0] aluResult,
  input  isLd,
  input  [31:0] op2,
  input  isSt,
  input  [31:0] InstructionEX,
  input  isCall,
  input  [31:0] PC,
  input  isWb,
  input  in_9,
  input  reset,
  output [31:0] aluResult_2,
  output isLd_2,
  output [31:0] op2_2,
  output isSt_2,
  output [31:0] InstructionMA,
  output isCall_2,
  output [31:0] PC_2,
  output isWb_2
);

  Register #(.width(32), .trigger("falling")) register_1 (
    .D(aluResult), .Q(aluResult_2), .clk(in_9), .clr(reset));  // open: en
  Register #(.width(32), .trigger("falling")) register_2 (.D(op2), .Q(op2_2), .clk(in_9), .clr(reset));  // open: en
  Register #(.width(32), .trigger("falling")) register_3 (
    .D(InstructionEX), .Q(InstructionMA), .clk(in_9), .clr(reset));  // open: en
  Register #(.width(32), .trigger("falling")) register_4 (.D(PC), .Q(PC_2), .clk(in_9), .clr(reset));  // open: en
  Register #(.width(1), .trigger("falling")) register_5 (.D(isLd), .Q(isLd_2), .clk(in_9), .clr(reset));  // open: en
  Register #(.width(1), .trigger("falling")) register_6 (.D(isSt), .Q(isSt_2), .clk(in_9), .clr(reset));  // open: en
  Register #(.width(1), .trigger("falling")) register_7 (
    .D(isCall), .Q(isCall_2), .clk(in_9), .clr(reset));  // open: en
  Register #(.width(1), .trigger("falling")) register_8 (.D(isWb), .Q(isWb_2), .clk(in_9), .clr(reset));  // open: en
endmodule

// MA-RW Latch
module MA_RWLatch (
  input  [31:0] aluResult,
  input  [31:0] ldResult,
  input  isLd,
  input  [31:0] InstructionMA,
  input  isCall,
  input  [31:0] PC,
  input  isWb,
  input  in_8,
  input  reset,
  output [31:0] aluResult_2,
  output [31:0] ldResult_2,
  output isLd_2,
  output [31:0] InstructionRW,
  output isCall_2,
  output [31:0] PC_2,
  output isWb_2
);

  Register #(.width(32), .trigger("falling")) register_1 (
    .D(aluResult), .Q(aluResult_2), .clk(in_8), .clr(reset));  // open: en
  Register #(.width(32), .trigger("falling")) register_2 (
    .D(ldResult), .Q(ldResult_2), .clk(in_8), .clr(reset));  // open: en
  Register #(.width(32), .trigger("falling")) register_3 (
    .D(InstructionMA), .Q(InstructionRW), .clk(in_8), .clr(reset));  // open: en
  Register #(.width(32), .trigger("falling")) register_4 (.D(PC), .Q(PC_2), .clk(in_8), .clr(reset));  // open: en
  Register #(.width(1), .trigger("falling")) register_5 (.D(isLd), .Q(isLd_2), .clk(in_8), .clr(reset));  // open: en
  Register #(.width(1), .trigger("falling")) register_6 (
    .D(isCall), .Q(isCall_2), .clk(in_8), .clr(reset));  // open: en
  Register #(.width(1), .trigger("falling")) register_7 (.D(isWb), .Q(isWb_2), .clk(in_8), .clr(reset));  // open: en
endmodule

module Data_Lock_Unit (
  input  [31:0] InstrIF_OF,
  input  [31:0] InstrOF_EX,
  output Stall
);

  wire comparator_1_eq, comparator_2_eq, isLd_out, or_1_out;

  Comparator #(.width(4)) comparator_1 (
    .a(InstrIF_OF[17:14]), .b(InstrOF_EX[25:22]), .eq(comparator_1_eq));  // open: gt, lt
  Comparator #(.width(4)) comparator_2 (
    .a(InstrIF_OF[21:18]), .b(InstrOF_EX[25:22]), .eq(comparator_2_eq));  // open: gt, lt
  or or_1 (or_1_out, comparator_1_eq, comparator_2_eq);
  and isLd (isLd_out, ~InstrOF_EX[27], InstrOF_EX[28], InstrOF_EX[29], InstrOF_EX[30], ~InstrOF_EX[31]);  // AND_Gate
  and and_1 (Stall, or_1_out, isLd_out);

  // Notes on the sheet:
  //   naya
  //   purana
  //   a
  //   b
  //   A.rs2
  //   A.rs1
  //   B.opcode
  //   Load Use hazard detector
  //   B.rd
endmodule

module Forwarding_Unit (
  input  [31:0] InstrIF_OF,
  input  [31:0] InstrOF_EX,
  input  [31:0] InstrEX_MA,
  input  [31:0] InstrMA_RW,
  output Mux1,
  output Mux2,
  output [1:0] Mux3,
  output [1:0] Mux4,
  output Mux5,
  output Mux6
);

  wire algo7_rs2_rdconflict_3_conflict_exists, isSt_out;

  Algo6_rs1_raconflict algo6_rs1_raconflict_1 (.A(InstrIF_OF), .B(InstrMA_RW), .conflictExists(Mux1));
  Algo7_rs2_rdconflict algo7_rs2_rdconflict_1 (.A(InstrIF_OF), .B(InstrMA_RW), .conflict_exists(Mux2));
  Algo6_rs1_raconflict algo6_rs1_raconflict_2 (.A(InstrOF_EX), .B(InstrMA_RW), .conflictExists(Mux3[0]));
  Algo7_rs2_rdconflict algo7_rs2_rdconflict_2 (.A(InstrOF_EX), .B(InstrMA_RW), .conflict_exists(Mux5));
  Algo6_rs1_raconflict algo6_rs1_raconflict_3 (.A(InstrOF_EX), .B(InstrEX_MA), .conflictExists(Mux3[1]));
  Algo7_rs2_rdconflict algo7_rs2_rdconflict_3 (
    .A(InstrOF_EX), .B(InstrEX_MA), .conflict_exists(algo7_rs2_rdconflict_3_conflict_exists));
  Algo7_rs2_rdconflict algo7_rs2_rdconflict_4 (.A(InstrEX_MA), .B(InstrMA_RW), .conflict_exists(Mux6));
  and isSt (isSt_out, ~InstrOF_EX[31], InstrOF_EX[30], InstrOF_EX[29], InstrOF_EX[28], InstrOF_EX[27]);  // AND_Gate
  Multiplexer #(.enable("false")) multiplexer_1 (
    .in0(algo7_rs2_rdconflict_3_conflict_exists), .in1(1'b0), .out(Mux4[1]), .sel(isSt_out));
  Multiplexer #(.enable("false")) multiplexer_2 (.in0(Mux5), .in1(1'b0), .out(Mux4[0]), .sel(isSt_out));
endmodule

// Algo6
module Algo6_rs1_raconflict (
  input  [31:0] A,
  input  [31:0] B,
  output conflictExists
);

  wire comparator_1_eq, isb_bgt_call_beq_out, isb_out, isbgt_beq_out, iscall_out, iscmp_out, ismov_not_out,
       isNop_2_out, isNop_out, isret_2_out, isret_out, isSt_out, or_1_out, or_2_out;
  wire [3:0] multiplexer_1_out, multiplexer_2_out;

  and isNop (isNop_out, ~A[31], A[30], A[29], ~A[28], A[27]);  // AND_Gate
  and ismov_not (ismov_not_out, ~A[31], A[30], ~A[29], ~A[28]);  // AND_Gate
  and isb_bgt_call_beq (isb_bgt_call_beq_out, A[31], ~A[30], ~A[29]);  // AND_Gate
  and isret (isret_out, A[31], ~A[30], A[29], ~A[28], ~A[27]);  // AND_Gate
  and iscall (iscall_out, B[31], ~B[30], ~B[29], B[28], B[27]);  // AND_Gate
  and isNop_2 (isNop_2_out, ~B[31], B[30], B[29], ~B[28], B[27]);  // AND_Gate
  and isbgt_beq (isbgt_beq_out, B[31], ~B[30], ~B[29], ~B[28]);  // AND_Gate
  and isb (isb_out, B[31], ~B[30], ~B[29], B[28], ~B[27]);  // AND_Gate
  and isret_2 (isret_2_out, B[31], ~B[30], B[29], ~B[28], ~B[27]);  // AND_Gate
  and iscmp (iscmp_out, ~B[31], ~B[30], B[29], ~B[28], B[27]);  // AND_Gate
  and isSt (isSt_out, ~B[31], B[30], B[29], B[28], B[27]);  // AND_Gate
  Multiplexer #(.width(4), .enable("false")) multiplexer_1 (
    .in0(A[21:18]), .in1(4'b1111), .out(multiplexer_1_out), .sel(isret_out));
  Multiplexer #(.width(4), .enable("false")) multiplexer_2 (
    .in0(B[25:22]), .in1(4'b1111), .out(multiplexer_2_out), .sel(iscall_out));
  or or_1 (or_1_out, isNop_out, ismov_not_out, isb_bgt_call_beq_out);
  or or_2 (or_2_out, isNop_2_out, isbgt_beq_out, isb_out, isret_2_out, iscmp_out, isSt_out);
  Comparator #(.width(4)) comparator_1 (
    .a(multiplexer_1_out), .b(multiplexer_2_out), .eq(comparator_1_eq));  // open: gt, lt
  and and_1 (conflictExists, ~or_1_out, comparator_1_eq, ~or_2_out);  // AND_Gate

  // Notes on the sheet:
  //   A.src1
  //   B.rd
  //   ra
  //   ra
  //   on rs1/ra
endmodule

// Algo7
module Algo7_rs2_rdconflict (
  input  [31:0] A,
  input  [31:0] B,
  output conflict_exists
);

  wire and_1_out, comparator_1_eq, isb_bgt_call_beq_out, isb_out, isbgt_beq_out, iscall_out, iscmp_out,
       isNop_2_out, isNop_out, isNOTSt_out, isret_out, isSt_out, not_1_out, or_1_out, or_2_out;
  wire [3:0] multiplexer_1_out, multiplexer_2_out;

  and isNop (isNop_out, ~A[31], A[30], A[29], ~A[28], A[27]);  // AND_Gate
  and isb_bgt_call_beq (isb_bgt_call_beq_out, A[31], ~A[30], ~A[29]);  // AND_Gate
  nand isNOTSt (isNOTSt_out, ~A[31], A[30], A[29], A[28], A[27]);  // NAND_Gate
  and iscall (iscall_out, B[31], ~B[30], ~B[29], B[28], B[27]);  // AND_Gate
  and isNop_2 (isNop_2_out, ~B[31], B[30], B[29], ~B[28], B[27]);  // AND_Gate
  and isbgt_beq (isbgt_beq_out, B[31], ~B[30], ~B[29], ~B[28]);  // AND_Gate
  and isb (isb_out, B[31], ~B[30], ~B[29], B[28], ~B[27]);  // AND_Gate
  and isret (isret_out, B[31], ~B[30], B[29], ~B[28], ~B[27]);  // AND_Gate
  and iscmp (iscmp_out, ~B[31], ~B[30], B[29], ~B[28], B[27]);  // AND_Gate
  and isSt (isSt_out, ~B[31], B[30], B[29], B[28], B[27]);  // AND_Gate
  or or_1 (or_1_out, isNop_out, isb_bgt_call_beq_out);
  and and_1 (and_1_out, isNOTSt_out, A[26]);
  not not_1 (not_1_out, isNOTSt_out);
  Multiplexer #(.width(4), .enable("false")) multiplexer_1 (
    .in0(B[25:22]), .in1(4'b1111), .out(multiplexer_1_out), .sel(iscall_out));
  Multiplexer #(.width(4), .enable("false")) multiplexer_2 (
    .in0(A[17:14]), .in1(A[25:22]), .out(multiplexer_2_out), .sel(not_1_out));
  or or_2 (or_2_out, isNop_2_out, isbgt_beq_out, isb_out, isret_out, iscmp_out, isSt_out);
  Comparator #(.width(4)) comparator_1 (
    .a(multiplexer_2_out), .b(multiplexer_1_out), .eq(comparator_1_eq));  // open: gt, lt
  and and_2 (conflict_exists, ~or_1_out, ~and_1_out, comparator_1_eq, ~or_2_out);  // AND_Gate

  // Notes on the sheet:
  //   A.src2
  //   B.rd
  //   ra
  //   src2
  //   on rs2/rd
endmodule
